// Logisim project Controleur.circ as structural Verilog
module main (
  input  FLAG,
  input  [31:0] SortirFromCheminDeDonnes,
  output [3:0] Ra,
  output [3:0] Rb,
  output [3:0] Rd,
  output [3:0] CodeOp
);

  wire Clock_out;
  wire [7:0] adder_1_out, bitselector_1_out, multiplexer_1_out, undriven;
  wire [15:0] rom_1_data;

  ROM #(.dataWidth(16)) rom_1 (.addr(adder_1_out), .data(rom_1_data));
  Register #(.width(16)) RI (.D(rom_1_data));  // open: en, clk, Q, clr
  Clock Clock (.out(Clock_out));
  Multiplexer #(.width(8), .enable("false")) multiplexer_1 (
    .in0(bitselector_1_out), .in1(undriven), .out(multiplexer_1_out));  // open: sel
  Adder adder_1 (.a(multiplexer_1_out), .b(8'h4), .out(adder_1_out));  // open: cin, cout
  Register PC (.D(adder_1_out), .clk(Clock_out), .Q(adder_1_out));  // open: en, clr
  BitSelector #(.width(32), .group(8)) bitselector_1 (
    .in(SortirFromCheminDeDonnes), .out(bitselector_1_out), .sel(2'b11));

  // Notes on the sheet:
  //   contents of rom_1 (hex, n*v repeats v):
  //   1 10 11 100 101 110 111 1000 1001 1011 1100 1101 1100 1101 1110 1111
endmodule

module Controleur (
  input  [5:0] DataProcessing,
  input  in_2,
  input  [15:0] PC
);

  wire and_1_out, comparator_1_eq;

  Comparator #(.width(6)) comparator_1 (.a(PC[15:10]), .b(DataProcessing), .eq(comparator_1_eq));  // open: gt, lt
  and and_1 (and_1_out, comparator_1_eq, in_2);
  Multiplexer #(.enable("false")) multiplexer_1 (.in0(and_1_out));  // open: in1, out, sel

  // Other names for the same wires on the sheet: OpCode[5:0] = PC[15:10]; b0 = PC[0]; b1 = PC[1]; b2 = PC[2];
  //   b3 = PC[3]; b4 = PC[4]; b5 = PC[5]; b6 = PC[6]; b7 = PC[7]; b8 = PC[8]; b9 = PC[9]
endmodule

module DataProcessing (
  input  [15:0] PC,
  input  in_2,
  input  in_3,
  output [2:0] Rd,
  output [2:0] Rn,
  output [2:0] Rm,
  output [3:0] ULACode,
  output [5:0] OpcodeData
);

  // AND_Gate and_1 has open pins: in0=PC[9], in1=in_2, out=open

  assign OpcodeData = PC[15:10];
  assign Rd = PC[2:0];
  assign Rm = PC[5:3];
  assign Rn = PC[2:0];
  assign ULACode = PC[9:6];

  // Other names for the same wires on the sheet: b6 = PC[6]; b7 = PC[7]; b8 = PC[8]; b9 = PC[9]
endmodule
